# Fritzing sketch LightSaber (saved by Fritzing 0.9.10b)
breadboards: 1

parts:
  U1 = attiny85 [package=dip]
  R1 = Rotary Potentiometer (Small) [maximum_resistance=100kΩ knob_status=50% power=0.5W package=THT]
  Part1 = ws2812b [package="smd 2812b"]
  CONN1 = USB connector [package=THT]

nets:
  N1: U1.Pin_2, Part1.DIN
  VSS: U1.Pin_4, R1.leg2, Part1.VSS, CONN1.GND, CONN1.chassis5, CONN1.chassis6
  N2: U1.Pin_7, R1.wiper
  VDD: U1.Pin_8, R1.leg1, Part1.VDD, CONN1.5V
